# Fritzing sketch turntable-mayen (saved by Fritzing 1.0.4)
breadboards: 1

parts:
  Part1 = Arduino Uno (Rev3)  # not connected
  Keypad4x1 = Keypad Membran 4x4
  Part2 = Adafruit Proto Shield R3 [part_number="Adafruit #2077"]
  SilentStepStick_TMC1 = SilentStepStick TMC2130 [package=SO16]
  M1 = Stepper Motor - Bipolar
  J1 = Screw terminal - 2 pins [package=THT]
  V1 = DC Power [voltage=9V internal_resistance=0.1Ω]
  J2 = female pin header, 4 pins [form="♀ (female)"]

nets:
  N1: Keypad4x1.Pin1, Part2.D13
  N2: Keypad4x1.Pin2, Part2.D12
  N3: Keypad4x1.Pin3, Part2.D11
  N4: Keypad4x1.Pin4, Part2.D10
  N5: Keypad4x1.Pin5, Part2.D9
  N6: Keypad4x1.Pin6, Part2.D8
  N7: Keypad4x1.Pin7, Part2.D7
  N8: Keypad4x1.Pin8, Part2.D6
  N9: Part2.VIN, SilentStepStick_TMC1.VMOT, J1.pin2, V1.V+
  N10: Part2.A0, J2.pin1
  N11: Part2.A1, J2.pin2
  N12: Part2.A2, J2.pin3
  N13: Part2.D4, SilentStepStick_TMC1.STEP
  N14: Part2.D5, SilentStepStick_TMC1.DIR
  N15: Part2.GND, SilentStepStick_TMC1.GND#14, J1.pin1, V1.V-, J2.pin4
  N16: Part2.+5V, SilentStepStick_TMC1.VIO
  N17: SilentStepStick_TMC1.1B, M1.D
  N18: SilentStepStick_TMC1.1A, M1.B
  N19: SilentStepStick_TMC1.2A, M1.C
  N20: SilentStepStick_TMC1.2B, M1.A

notes:
  2xblue: outer track pins,
  yellow: all other track pins,
  black: ground, connect to green turntable wire.

custom parts:
  Keypad Membran 4x4: Membrane Keypad 4x4 Matrix
  Adafruit Proto Shield R3: This prototyping shield is the best out there (well, we think so, at least), and now is even better with Version R3 - updated for the most compatibility with just about all the Arduinos! It works with UNO, Mega, Leonardo, NG, Diecimila, Duemilanove, and compatible Arduinos. Yun's and Arduino Ethernets have a chunky Ethernet jack that gets in the way of stacking, you can use the stacking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
  SilentStepStick TMC2130: The TMC2130 provides an integrated motor driver solution for 3D-Printing, Cameras, Scanners and other automated equipment applications. The device has an integrated microstepping indexer, the sensorless stall detection technology StallGuard2™, the sensorless load dependent current control CoolStep™ and the completely noiseless current control mode StealthChop™ and is intended to drive a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
